// Logisim project ALOVT_ALL_TASKS.circ as structural Verilog: 3 circuits, main circuit Задание 1
module \Задание_1  (
  input  v,
  input  x0,
  input  x1,
  input  [2:0] in_4,
  input  x3,
  output q0,
  output q1,
  output q2,
  output q3,
  output q4,
  output q5,
  output q6,
  output q7
);

  Demultiplexer #(.select(3)) demultiplexer_1 (
    .out0(q0), .out1(q1), .out2(q2), .out3(q3), .out4(q4), .out5(q5), .out6(q6), .out7(q7), .in(v), .sel(in_4));  // open: en

  assign x0 = in_4[0];
  assign x1 = in_4[1];
  assign x3 = in_4[2];
endmodule

module \Задание_3  (
  input  x1,
  input  x2,
  input  x3,
  output y1,
  output y2,
  output y3
);

  wire not_1_out, not_2_out, not_3_out, not_4_out, not_5_out, not_6_out, not_7_out, not_8_out, not_9_out,
       or_1_out, or_2_out, or_3_out, or_4_out;

  not not_1 (not_1_out, x2);
  not not_2 (not_2_out, x1);
  not not_3 (not_3_out, x1);
  not not_4 (not_4_out, x2);
  not not_5 (not_5_out, x3);
  or or_1 (or_1_out, x1, not_1_out);
  not not_6 (not_6_out, or_1_out);
  not not_7 (not_7_out, or_2_out);
  or or_2 (or_2_out, x2, not_2_out);
  not not_8 (not_8_out, or_3_out);
  or or_3 (or_3_out, not_3_out, not_4_out);
  or or_4 (or_4_out, x1, x2, x3);
  not not_9 (not_9_out, or_4_out);
  or or_5 (y2, x1, x2, not_5_out);
  or or_6 (y3, not_6_out, not_7_out);
  or or_7 (y1, not_8_out, not_9_out);
endmodule

module \Задание_2  (
  input  v,
  input  x0,
  input  x1,
  output q0,
  output q1,
  output q2,
  output q3
);

  wire not_1_out, not_2_out, not_3_out, not_4_out;

  not not_1 (not_1_out, x0);
  and and_1 (q0, v, not_1_out, not_2_out);
  not not_2 (not_2_out, x1);
  and and_2 (q1, v, x0, not_3_out);
  not not_3 (not_3_out, x1);
  not not_4 (not_4_out, x0);
  and and_3 (q2, not_4_out, x1, v);
  and and_4 (q3, x0, x1, v);
endmodule
